// Logisim project wet_van_more_ofz.circ as structural Verilog: 1 circuit, main circuit main
module main (
);

  wire and_1_out, dipswitch_1_sw1, dipswitch_1_sw2, not_1_out, not_2_out, not_3_out, or_1_out;

  DipSwitch dipswitch_1 (.sw1(dipswitch_1_sw1), .sw2(dipswitch_1_sw2));  // open: sw3, sw4, sw5, sw6, sw7, sw8
  not not_1 (not_1_out, dipswitch_1_sw2);
  not not_2 (not_2_out, dipswitch_1_sw1);
  and and_1 (and_1_out, dipswitch_1_sw1, dipswitch_1_sw2);
  not not_3 (not_3_out, and_1_out);
  // AND_Gate and_2 is placed but not wired
  or or_1 (or_1_out, not_1_out, not_2_out);
  LED led_1 (.in(or_1_out));
  LED led_2 (.in(not_3_out));
endmodule
